# Fritzing sketch Project_1(Fritzing) (saved by Fritzing 0.9.9b)
breadboards: 1

parts:
  D1 = LED_BARGRAPH_10 [package=led_bargaph_10]
  S1 = Pushbutton [package="[SMD]"]
  S2 = Pushbutton [package="[SMD]"]
  R1 = Resistor [tolerance=±5% resistance=220 package="0402 [SMD]"]
  R2 = Resistor [tolerance=±5% resistance=220 package="0402 [SMD]"]
  R3 = Resistor [tolerance=±5% resistance=220 package="0402 [SMD]"]
  R4 = Resistor [tolerance=±5% resistance=220 package="0402 [SMD]"]
  R6 = Resistor [tolerance=±5% resistance=220 package="0402 [SMD]"]
  R7 = Resistor [tolerance=±5% resistance=220 package="0402 [SMD]"]
  R8 = Resistor [tolerance=±5% resistance=220 package="0402 [SMD]"]
  R9 = Resistor [tolerance=±5% resistance=220 package="0402 [SMD]"]
  R10 = Resistor [tolerance=±5% resistance=220 package="0402 [SMD]"]
  R12 = Resistor [tolerance=±5% resistance=220 package="0402 [SMD]"]
  R13 = Resistor [tolerance=±5% resistance=220 package="0402 [SMD]"]
  R14 = Resistor [tolerance=±5% resistance=220 package="0402 [SMD]"]

nets:
  N1: D1.A_A, R9.Pin_1
  N2: D1.B_A, R8.Pin_1
  N3: D1.C_A, R7.Pin_1
  N4: D1.D_A, R6.Pin_1
  N5: D1.E_A, R10.Pin_1
  N6: D1.F_A, R13.Pin_1
  N7: D1.G_A, R12.Pin_1
  N8: D1.H_A, R14.Pin_1
  N9: D1.F_C, D1.A_C
  N10: S1.Pin_1, S1.Pin_2, S2.Pin_1, S2.Pin_2, R6.Pin_0, R7.Pin_0, R8.Pin_0, R9.Pin_0, R10.Pin_0, R12.Pin_0, R13.Pin_0, R14.Pin_0
  N11: S1.Pin_3, S1.Pin_4, R1.Pin_1, R3.Pin_0
  N12: S2.Pin_3, S2.Pin_4, R2.Pin_1, R4.Pin_0
  N13: R3.Pin_1, R4.Pin_1
